# Fritzing sketch MSP430G2553 (saved by Fritzing 0.9.3b)
breadboards: 1

parts:
  IC1 = IC, DIP package, 20 pins [chip_label=MSP430G2553 part_number=MSP430G2553]
  LED1 = LED - 5mm [color="Red (633nm)" package="5 mm [THT]"]
  LED2 = LED - 5mm [color="Green (555nm)" package="5 mm [THT]"]
  R2 = Resistor [tolerance=±5% resistance=220 package=THT]
  R3 = Resistor [tolerance=±5% resistance=47k package=THT]
  R1 = Resistor [tolerance=±5% resistance=220 package=THT]
  J1 = female pin header, 2 pins [form="♀ (female)"]
  J2 = female pin header, 2 pins [form="♀ (female)"]
  C1 = Electrolytic Capacitor [capacitance=1µF package="100 mil [THT, electrolytic]"]
  S1 = Pushbutton [package="[THT]"]
  C2 = Ceramic Capacitor [capacitance=1nF package="100 mil [THT, multilayer]"]

nets:
  3.3V: IC1.pin1, LED1.anode, R3.Pin_0, J1.pin1, C1.+
  N1: IC1.pin2, LED2.anode
  N2: IC1.pin16, R3.Pin_1, J2.pin2, S1.Pin_1, S1.Pin_2, C2.1
  N3: IC1.pin17, J2.pin1
  GND: IC1.pin20, R2.Pin_0, R1.Pin_0, J1.pin2, C1.-, S1.Pin_3, S1.Pin_4, C2.0
  N4: LED1.cathode, R1.Pin_1
  N5: LED2.cathode, R2.Pin_1

notes:
  Power LED
  User LED (on P1.0)
  Reset
  Pwr
  Gnd
  SBWTCK
  SBWTDIO
  Pwr (2.2-3.6V)
