# Fritzing sketch PIC16F18446 (saved by Fritzing 0.9.3b)
breadboards: 1

parts:
  IC1 = IC, DIP package, 20 pins [chip_label=PIC16F18446]
  C1 = Electrolytic Capacitor [capacitance=100nF package="100 mil [THT, electrolytic]"]
  R3 = Resistor [tolerance=±10% resistance=10k package=THT]
  LED2 = LED - 5mm [color="Green (555nm)" package="5 mm [THT]"]
  LED1 = LED - 5mm [color="Red (633nm)" package="5 mm [THT]"]
  R1 = Resistor [tolerance=±5% resistance=220 package=THT]
  R2 = Resistor [tolerance=±5% resistance=220 package=THT]
  J2 = female pin header, 5 pins [form="♀ (female)"]
  J1 = female pin header, 2 pins [form="♀ (female)"]
  C2 = Ceramic Capacitor [capacitance=10nF package="100 mil [THT, multilayer]"]
  R4 = Resistor [tolerance=±5% resistance=220 package=THT]
  S1 = Pushbutton [package="[THT]"]

nets:
  5V: IC1.pin1, C1.+, R3.Pin_1, LED1.anode, J2.pin2, J1.pin1
  N1: IC1.pin2, LED2.anode
  N2: IC1.pin4, R4.Pin_0
  N3: IC1.pin18, J2.pin5
  N4: IC1.pin19, J2.pin4
  GND: IC1.pin20, C1.-, R1.Pin_1, R2.Pin_1, J2.pin3, J1.pin2, C2.1, S1.Pin_1, S1.Pin_2
  N5: R3.Pin_0, J2.pin1, C2.0, R4.Pin_1, S1.Pin_3, S1.Pin_4
  N6: LED2.cathode, R2.Pin_0
  N7: LED1.cathode, R1.Pin_0

notes:
  Gnd
  Pwr
  Reset
  Power LED
  User LED (on RA5)
  nMCLR
  V_DD
  GND
  PGD
  PGC
  Pwr (2.5-5.5V)
