# Fritzing sketch dsPIC33EV32GM002 (saved by Fritzing 0.9.3b)
breadboards: 1

parts:
  J2 = female pin header, 2 pins [form="♀ (female)"]
  C1 = Electrolytic Capacitor [capacitance=100nF package="100 mil [THT, electrolytic]"]
  J3 = female pin header, 5 pins [form="♀ (female)"]
  IC1 = IC, DIP package, 28 pins [chip_label=dsPIC33EV32GM002]
  C5 = Tantalum Capacitor [capacitance=1μF package="100 mil [THT, tantalum]"]
  C3 = Ceramic Capacitor [capacitance=100nF package="100 mil [THT, multilayer]"]
  C4 = Ceramic Capacitor [capacitance=100nF package="100 mil [THT, multilayer]"]
  LED2 = LED - 5mm [color="Green (555nm)" package="5 mm [THT]"]
  LED1 = LED - 5mm [color="Red (633nm)" package="5 mm [THT]"]
  R2 = Resistor [tolerance=±5% resistance=220 package=THT]
  R1 = Resistor [tolerance=±5% resistance=220 package=THT]
  S1 = Pushbutton [package="[THT]"]
  C2 = Ceramic Capacitor [capacitance=100nF package="100 mil [THT, multilayer]"]
  R4 = Resistor [tolerance=±5% resistance=220 package=THT]
  R3 = Resistor [tolerance=±5% resistance=10k package=THT]

nets:
  5V: J2.pin1, C1.+, J3.pin2, IC1.pin13, IC1.pin28, C3.1, C4.0, R2.Pin_1, R1.Pin_1, R3.Pin_1
  GND: J2.pin2, C1.-, J3.pin3, IC1.pin8, IC1.pin19, IC1.pin27, C5.-, C3.0, C4.1, LED1.cathode, S1.Pin_1, S1.Pin_2, C2.1
  N1: J3.pin1, S1.Pin_3, S1.Pin_4, C2.0, R4.Pin_0, R3.Pin_0
  N2: J3.pin4, IC1.pin7
  N3: J3.pin5, IC1.pin6
  N4: IC1.pin1, R4.Pin_1
  N5: IC1.pin2, LED2.cathode
  N6: IC1.pin20, C5.+
  N7: LED2.anode, R2.Pin_0
  N8: LED1.anode, R1.Pin_0

notes:
  Gnd
  Pwr
  PGC
  PGD
  GND
  V_DD
  nMCLR
  Power LED
  User LED (on RA0)
  Pwr (4.6-5.5V)
